# Fritzing sketch CREPO3CirCuit (saved by Fritzing 0.9.4)
breadboards: 1

parts:
  A1 = Weewooday 1.5-4.2 to 5v stepup converter [package=THT]
  A2 = olimex ESP32-POE-ISO
  RFID1 = RFID Reader
  Bauteil1 = I2C level shifter bidirectional
  BAT1 = 18650 battery holder [package=battery-18650-kit]
  S1 = Taiway 100-SP-X-T1 SPDT Miniature Toggle Switch [part_number=100-SP-X-T1-0-0-B1-M2 package=THT]
  S2 = Taiway 100-SP-X-T1 SPDT Miniature Toggle Switch [part_number=100-SP-X-T1-0-0-B1-M2 package=THT]

nets:
  N1: A1.pin1, A2.Pin_2, Bauteil1.LV
  GND: A1.pin2, A2.Pin_3, A2.Pin_32, RFID1.GND, Bauteil1.GND, S2.L1
  N2: A1.pin3, RFID1.+5V, Bauteil1.HV
  N3: A2.Pin_5, S2.COM
  N4: A2.Pin_7, Bauteil1.LV4
  N5: A2.Pin_8, Bauteil1.LV3
  N6: A2.Pin_9, Bauteil1.LV2
  N7: A2.Pin_10, Bauteil1.LV1
  N8: A2.Pin_11, S1.L1
  N9: A2.Pin_12, BAT1.-
  N10: RFID1.+/-, Bauteil1.HV3
  N11: RFID1.D1, Bauteil1.HV2
  N12: RFID1.D0, Bauteil1.HV1
  N13: RFID1.LED, Bauteil1.HV4
  N14: BAT1.+, S1.COM

notes:
  MODE_SWITCH 0 //cyan
  RFID_D0 5 //Yellow
  RFID_D1 4 //Green
  LED 3 //Blue
  BUZZER 2 //Orange

custom parts:
  Weewooday 1.5-4.2 to 5v stepup converter: Weewooday 1.5-4.2 to 5v stepup converter.
  olimex ESP32-POE-ISO: ESP32-PoE is an IoT WIFI/BLE/Ethernet development board with Power-Over-Ethernet feature.
  I2C level shifter bidirectional: This is an interface board to connect 5V I2C to 3V I2C. It is bidirectinal.
  18650 battery holder: 18650 Battery Holder
